# Fritzing sketch IRTest (saved by Fritzing 0.9.2b)
breadboards: 1

parts:
  Part1 = Arduino Nano (Rev3.0)
  IR1 = TSOP312.., 314.. [package=THT]
  LED1 = LED - 5mm [color="Red (633nm)" package="5 mm [THT]"]
  R1 = Resistor [tolerance=±5% resistance=220 package=THT]

nets:
  N1: Part1.GND, IR1.Vs, R1.Pin_0
  N2: Part1.D8, LED1.anode
  N3: Part1.D11/MOSI, IR1.GND
  N4: Part1.3V3, IR1.Data
  N5: LED1.cathode, R1.Pin_1
